// Logisim project 0 1 4.circ as structural Verilog: 3 circuits, main circuit main
module main (
  input  in_1,
  output out_2,
  output out_3,
  output out_4
);

  wire bcd_1_a_2, bcd_1_b_2, bcd_1_c_2, bcd_1_d_2, bcd_1_e, bcd_1_f, bcd_1_g, clock_1_out, n1_1_j0, n1_1_j1,
       n1_1_j2, n1_1_k0, n1_1_k1, n1_1_k2;

  Clock clock_1 (.out(clock_1_out));
  J_K_Flip_Flop j_k_ff_1 (.J(n1_1_k2), .clk(clock_1_out), .K(n1_1_j2), .Q(out_2));  // open: Qn, preset, en, reset
  J_K_Flip_Flop j_k_ff_2 (.J(n1_1_j1), .clk(clock_1_out), .K(n1_1_k1), .Q(out_3));  // open: Qn, preset, en, reset
  _1 u_1_1 (
    .Q2(out_2), .Q1(out_3), .Q0(out_4), .J2(n1_1_j2), .K2(n1_1_k2), .J1(n1_1_j1), .K1(n1_1_k1), .J0(n1_1_j0),
    .K0(n1_1_k0));
  J_K_Flip_Flop j_k_ff_3 (.J(n1_1_j0), .clk(clock_1_out), .K(n1_1_k0), .Q(out_4));  // open: Qn, preset, en, reset
  BCD bcd_1 (
    .D(in_1), .C(out_2), .B(out_3), .A(out_4), .g(bcd_1_g), .f(bcd_1_f), .e(bcd_1_e), .d_2(bcd_1_d_2),
    .c_2(bcd_1_c_2), .b_2(bcd_1_b_2), .a_2(bcd_1_a_2));  // open: h
  _7_Segment_Display u_7_segment_display_1 (
    .g(bcd_1_g), .f(bcd_1_f), .a(bcd_1_a_2), .b(bcd_1_b_2), .e(bcd_1_e), .d(bcd_1_d_2), .c(bcd_1_c_2));  // open: dp
endmodule

module _1 (
  input  Q2,
  input  Q1,
  input  Q0,
  output J2,
  output K2,
  output J1,
  output K1,
  output J0,
  output K0
);

  wire and_1_out, and_2_out, not_1_out, not_2_out, not_3_out, not_4_out;

  not not_1 (not_1_out, Q1);
  not not_2 (not_2_out, Q0);
  not not_3 (not_3_out, Q2);
  not not_4 (not_4_out, Q2);
  and and_1 (and_1_out, not_1_out, not_2_out);
  and and_2 (and_2_out, Q1, Q0);
  or or_1 (J0, not_3_out, Q1);
  or or_2 (K0, not_4_out, Q1);
  or or_3 (J2, and_1_out, and_2_out);

  assign J1 = Q2;
  assign K1 = Q2;
  assign K2 = Q0;
endmodule

module BCD (
  input  D,
  input  C,
  input  B,
  input  A,
  output h,
  output g,
  output f,
  output e,
  output d_2,
  output c_2,
  output b_2,
  output a_2
);

  wire and_1_out, and_2_out, and_3_out, and_4_out, and_5_out, and_6_out, and_7_out, and_8_out, and_9_out,
       and_10_out, and_11_out, and_12_out, and_13_out, and_14_out, and_15_out, and_16_out, and_17_out,
       and_18_out, and_19_out, and_20_out, and_21_out, and_22_out, and_23_out, and_24_out, and_25_out,
       and_26_out, and_27_out, and_28_out, and_29_out, and_30_out, and_31_out, and_32_out, and_33_out,
       and_34_out, and_35_out, not_1_out, not_2_out, not_3_out, not_4_out, not_5_out, not_6_out, not_7_out,
       not_8_out, not_9_out, not_10_out, not_11_out, not_12_out, not_13_out, not_14_out, not_15_out,
       not_16_out, not_17_out, not_18_out, not_19_out, not_20_out, not_21_out, not_22_out, not_23_out,
       not_24_out, not_25_out, not_26_out, not_27_out, not_28_out, not_29_out, not_30_out, not_31_out,
       not_32_out, not_33_out, not_34_out, not_35_out, not_36_out, not_37_out, not_38_out, not_39_out,
       not_40_out, not_41_out, not_42_out, not_43_out, not_44_out;

  not not_1 (not_1_out, C);
  and and_1 (and_1_out, not_1_out, B);
  and and_2 (and_2_out, B, not_2_out);
  not not_2 (not_2_out, A);
  not not_3 (not_3_out, D);
  and and_3 (and_3_out, not_3_out, C, not_4_out);
  not not_4 (not_4_out, B);
  and and_4 (and_4_out, D, not_5_out);
  not not_5 (not_5_out, C);
  and and_5 (and_5_out, D, A);
  not not_6 (not_6_out, B);
  and and_6 (and_6_out, not_6_out, not_7_out);
  not not_7 (not_7_out, A);
  not not_8 (not_8_out, D);
  and and_7 (and_7_out, not_8_out, C, not_9_out);
  not not_9 (not_9_out, B);
  and and_8 (and_8_out, C, not_10_out);
  not not_10 (not_10_out, A);
  and and_9 (and_9_out, D, not_11_out);
  not not_11 (not_11_out, C);
  and and_10 (and_10_out, D, B);
  not not_12 (not_12_out, C);
  and and_11 (and_11_out, not_12_out, not_13_out);
  not not_13 (not_13_out, A);
  and and_12 (and_12_out, B, not_14_out);
  not not_14 (not_14_out, A);
  and and_13 (and_13_out, D, B);
  and and_14 (and_14_out, D, C);
  not not_15 (not_15_out, D);
  and and_15 (and_15_out, not_15_out, not_16_out, not_17_out);
  not not_16 (not_16_out, C);
  not not_17 (not_17_out, A);
  not not_18 (not_18_out, C);
  and and_16 (and_16_out, not_18_out, B, A);
  not not_19 (not_19_out, B);
  and and_17 (and_17_out, C, not_19_out, A);
  and and_18 (and_18_out, C, B, not_20_out);
  not not_20 (not_20_out, A);
  not not_21 (not_21_out, B);
  and and_19 (and_19_out, D, not_21_out, not_22_out);
  not not_22 (not_22_out, A);
  not not_23 (not_23_out, D);
  and and_20 (and_20_out, not_23_out, not_24_out);
  not not_24 (not_24_out, B);
  not not_25 (not_25_out, D);
  and and_21 (and_21_out, not_25_out, A);
  not not_26 (not_26_out, B);
  and and_22 (and_22_out, not_26_out, A);
  not not_27 (not_27_out, D);
  and and_23 (and_23_out, not_27_out, C);
  and and_24 (and_24_out, D, not_28_out);
  not not_28 (not_28_out, C);
  not not_29 (not_29_out, D);
  and and_25 (and_25_out, not_29_out, not_30_out);
  not not_30 (not_30_out, C);
  not not_31 (not_31_out, D);
  not not_32 (not_32_out, B);
  and and_26 (and_26_out, not_31_out, not_32_out, not_33_out);
  not not_33 (not_33_out, A);
  not not_34 (not_34_out, C);
  and and_27 (and_27_out, not_34_out, not_35_out);
  not not_35 (not_35_out, A);
  not not_36 (not_36_out, D);
  and and_28 (and_28_out, not_36_out, B, A);
  not not_37 (not_37_out, B);
  and and_29 (and_29_out, D, not_37_out, A);
  not not_38 (not_38_out, C);
  and and_30 (and_30_out, not_38_out, not_39_out);
  not not_39 (not_39_out, A);
  not not_40 (not_40_out, D);
  and and_31 (and_31_out, not_40_out, B);
  not not_41 (not_41_out, D);
  and and_32 (and_32_out, not_41_out, C, A);
  and and_33 (and_33_out, C, B);
  and and_34 (and_34_out, D, not_42_out, not_43_out);
  not not_42 (not_42_out, C);
  not not_43 (not_43_out, B);
  and and_35 (and_35_out, D, not_44_out);
  not not_44 (not_44_out, A);
  or or_1 (g, and_1_out, and_2_out, and_3_out, and_4_out, and_5_out);
  or or_2 (f, and_6_out, and_7_out, and_8_out, and_9_out, and_10_out);
  or or_3 (e, and_11_out, and_12_out, and_13_out, and_14_out);
  or or_4 (d_2, and_15_out, and_16_out, and_17_out, and_18_out, and_19_out);
  or or_5 (c_2, and_20_out, and_21_out, and_22_out, and_23_out, and_24_out);
  or or_6 (b_2, and_25_out, and_26_out, and_27_out, and_28_out, and_29_out);
  or or_7 (a_2, and_30_out, and_31_out, and_32_out, and_33_out, and_34_out, and_35_out);

  assign h = 1'b0;
endmodule
