// Logisim project CIR1.circ as structural Verilog: 3 circuits, main circuit main
module main (
  input  A,
  input  B,
  input  C,
  output R,
  output E
);

  wire and_1_out, and_2_out, and_3_out, and_4_out, and_5_out, and_6_out, and_7_out, not_1_out, not_2_out,
       not_3_out, not_4_out, not_5_out, not_6_out;

  not not_1 (not_1_out, A);
  not not_2 (not_2_out, B);
  not not_3 (not_3_out, A);
  not not_4 (not_4_out, C);
  not not_5 (not_5_out, B);
  not not_6 (not_6_out, C);
  and and_1 (and_1_out, B, C);
  and and_2 (and_2_out, A, C);
  and and_3 (and_3_out, A, B);
  and and_4 (and_4_out, not_1_out, not_2_out, C);
  and and_5 (and_5_out, not_3_out, B, not_4_out);
  and and_6 (and_6_out, A, not_5_out, not_6_out);
  and and_7 (and_7_out, A, B, C);
  or or_1 (E, and_1_out, and_2_out, and_3_out);
  or or_2 (R, and_4_out, and_5_out, and_6_out, and_7_out);
endmodule

module SUM (
  input  B2,
  input  B1,
  input  B0,
  input  A2,
  input  A1,
  input  A0,
  output out_7,
  output out_8,
  output out_9,
  output out_10
);

  wire main_2_e, main_3_e, n7seg_1_a_2, n7seg_1_b_2, n7seg_1_c_2, n7seg_1_d_2, n7seg_1_e, n7seg_1_f,
       n7seg_1_g;

  main main_1 (.A(A2), .B(B2), .C(main_2_e), .R(out_8), .E(out_7));
  main main_2 (.A(A1), .B(B1), .C(main_3_e), .R(out_9), .E(main_2_e));
  _7SEG u_7seg_1 (
    .A(out_7), .B(out_8), .C(out_9), .D(out_10), .a_2(n7seg_1_a_2), .b_2(n7seg_1_b_2), .c_2(n7seg_1_c_2),
    .d_2(n7seg_1_d_2), .e(n7seg_1_e), .f(n7seg_1_f), .g(n7seg_1_g));
  _7_Segment_Display u_7_segment_display_1 (
    .g(n7seg_1_g), .f(n7seg_1_f), .a(n7seg_1_a_2), .b(n7seg_1_b_2), .e(n7seg_1_e), .d(n7seg_1_d_2),
    .c(n7seg_1_c_2));  // open: dp
  main main_3 (.A(A0), .B(B0), .C(1'b0), .R(out_10), .E(main_3_e));
endmodule

module _7SEG (
  input  A,
  input  B,
  input  C,
  input  D,
  output a_2,
  output b_2,
  output c_2,
  output d_2,
  output e,
  output f,
  output g
);

  wire and_1_out, and_2_out, and_3_out, and_4_out, and_5_out, and_6_out, and_7_out, and_8_out, and_9_out,
       and_10_out, and_11_out, and_12_out, and_13_out, and_14_out, and_15_out, and_16_out, and_17_out,
       and_18_out, and_19_out, and_20_out, and_21_out, and_22_out, and_23_out, and_24_out, and_25_out,
       and_26_out, and_27_out, and_28_out, and_29_out, and_30_out, and_31_out, and_32_out, and_33_out,
       and_34_out, and_35_out, not_1_out, not_2_out, not_3_out, not_4_out, not_5_out, not_6_out, not_7_out,
       not_8_out, not_9_out, not_10_out, not_11_out, not_12_out, not_13_out, not_14_out, not_15_out,
       not_16_out, not_17_out, not_18_out, not_19_out, not_20_out, not_21_out, not_22_out, not_23_out,
       not_24_out, not_25_out, not_26_out, not_27_out, not_28_out, not_29_out, not_30_out, not_31_out,
       not_32_out, not_33_out, not_34_out, not_35_out, not_36_out, not_37_out, not_38_out, not_39_out,
       not_40_out, not_41_out, not_42_out, not_43_out, not_44_out;

  not not_1 (not_1_out, B);
  and and_1 (and_1_out, not_1_out, not_2_out);
  not not_2 (not_2_out, D);
  not not_3 (not_3_out, A);
  and and_2 (and_2_out, not_3_out, C);
  not not_4 (not_4_out, A);
  and and_3 (and_3_out, not_4_out, B, D);
  and and_4 (and_4_out, B, C);
  not not_5 (not_5_out, B);
  and and_5 (and_5_out, A, not_5_out, not_6_out);
  not not_6 (not_6_out, C);
  and and_6 (and_6_out, A, not_7_out);
  not not_7 (not_7_out, D);
  not not_8 (not_8_out, A);
  and and_7 (and_7_out, not_8_out, not_9_out);
  not not_9 (not_9_out, B);
  not not_10 (not_10_out, A);
  and and_8 (and_8_out, not_10_out, not_11_out, not_12_out);
  not not_11 (not_11_out, C);
  not not_12 (not_12_out, D);
  not not_13 (not_13_out, B);
  and and_9 (and_9_out, not_13_out, not_14_out);
  not not_14 (not_14_out, D);
  not not_15 (not_15_out, A);
  and and_10 (and_10_out, not_15_out, C, D);
  not not_16 (not_16_out, C);
  and and_11 (and_11_out, A, not_16_out, D);
  not not_17 (not_17_out, A);
  and and_12 (and_12_out, not_17_out, not_18_out);
  not not_18 (not_18_out, C);
  not not_19 (not_19_out, A);
  and and_13 (and_13_out, not_19_out, D);
  not not_20 (not_20_out, C);
  and and_14 (and_14_out, not_20_out, D);
  not not_21 (not_21_out, A);
  and and_15 (and_15_out, not_21_out, B);
  and and_16 (and_16_out, A, not_22_out);
  not not_22 (not_22_out, B);
  not not_23 (not_23_out, A);
  and and_17 (and_17_out, not_23_out, not_24_out, not_25_out);
  not not_24 (not_24_out, B);
  not not_25 (not_25_out, D);
  not not_26 (not_26_out, B);
  and and_18 (and_18_out, not_26_out, C, D);
  and and_19 (and_19_out, B, not_27_out, D);
  not not_27 (not_27_out, C);
  and and_20 (and_20_out, B, C, not_28_out);
  not not_28 (not_28_out, D);
  not not_29 (not_29_out, C);
  and and_21 (and_21_out, A, not_29_out, not_30_out);
  not not_30 (not_30_out, D);
  not not_31 (not_31_out, B);
  and and_22 (and_22_out, not_31_out, not_32_out);
  not not_32 (not_32_out, D);
  and and_23 (and_23_out, C, not_33_out);
  not not_33 (not_33_out, D);
  and and_24 (and_24_out, A, C);
  and and_25 (and_25_out, A, B);
  not not_34 (not_34_out, C);
  and and_26 (and_26_out, not_34_out, not_35_out);
  not not_35 (not_35_out, D);
  not not_36 (not_36_out, A);
  and and_27 (and_27_out, not_36_out, B, not_37_out);
  not not_37 (not_37_out, C);
  and and_28 (and_28_out, B, not_38_out);
  not not_38 (not_38_out, D);
  and and_29 (and_29_out, A, not_39_out);
  not not_39 (not_39_out, B);
  and and_30 (and_30_out, A, C);
  not not_40 (not_40_out, B);
  and and_31 (and_31_out, not_40_out, C);
  and and_32 (and_32_out, C, not_41_out);
  not not_41 (not_41_out, D);
  not not_42 (not_42_out, A);
  and and_33 (and_33_out, not_42_out, B, not_43_out);
  not not_43 (not_43_out, C);
  and and_34 (and_34_out, A, not_44_out);
  not not_44 (not_44_out, B);
  and and_35 (and_35_out, A, D);
  or or_1 (b_2, and_7_out, and_8_out, and_9_out, and_10_out, and_11_out);
  or or_2 (c_2, and_12_out, and_13_out, and_14_out, and_15_out, and_16_out);
  or or_3 (d_2, and_17_out, and_18_out, and_19_out, and_20_out, and_21_out);
  or or_4 (e, and_22_out, and_23_out, and_24_out, and_25_out);
  or or_5 (f, and_26_out, and_27_out, and_28_out, and_29_out, and_30_out);
  or or_6 (g, and_31_out, and_32_out, and_33_out, and_34_out, and_35_out);
  or or_7 (a_2, and_1_out, and_2_out, and_3_out, and_4_out, and_5_out, and_6_out);
endmodule
