// Logisim project bcd.circ as structural Verilog: 2 circuits, main circuit main
module main (
  output out_1
);

  wire undriven, undriven_2, undriven_3, undriven_4, undriven_5, undriven_6, undriven_7, undriven_8,
       undriven_9, undriven_10, undriven_11, undriven_12, undriven_13, undriven_14;

  comparador comparador_1 (
    .A(1'b0), .B(1'b0), .C(1'b0), .D(1'b0), .a_2(out_1), .b_2(undriven_4), .c_2(undriven_3), .d_2(undriven));
  comparador comparador_2 (.A(undriven_4), .B(undriven_3), .C(undriven), .D(undriven_2));  // open: a_2, b_2, c_2, d_2
  comparador comparador_3 ();  // open: A, B, C, D, a_2, b_2, c_2, d_2
  comparador comparador_4 ();  // open: A, B, C, D, a_2, b_2, c_2, d_2
  comparador comparador_5 ();  // open: A, B, C, D, a_2, b_2, c_2, d_2
  comparador comparador_6 ();  // open: A, B, C, D, a_2, b_2, c_2, d_2
  comparador comparador_7 ();  // open: A, B, C, D, a_2, b_2, c_2, d_2
  comparador comparador_8 (
    .A(1'b0), .B(1'b0), .C(1'b0), .D(1'b0), .a_2(undriven_2), .b_2(undriven_7), .c_2(undriven_6),
    .d_2(undriven_5));
  comparador comparador_9 (
    .A(undriven_7), .B(undriven_6), .C(undriven_5), .D(undriven_14));  // open: a_2, b_2, c_2, d_2
  comparador comparador_10 ();  // open: A, B, C, D, a_2, b_2, c_2, d_2
  comparador comparador_11 ();  // open: A, B, C, D, a_2, b_2, c_2, d_2
  comparador comparador_12 ();  // open: A, B, C, D, a_2, b_2, c_2, d_2
  comparador comparador_13 ();  // open: A, B, C, D, a_2, b_2, c_2, d_2
  comparador comparador_14 ();  // open: A, B, C, D, a_2, b_2, c_2, d_2
  comparador comparador_15 (
    .A(1'b0), .B(1'b0), .C(1'b1), .D(1'b1), .a_2(undriven_14), .b_2(undriven_12), .c_2(undriven_10),
    .d_2(undriven_8));
  comparador comparador_16 (
    .A(undriven_12), .B(undriven_10), .C(undriven_8), .D(1'b1), .b_2(undriven_13), .c_2(undriven_11),
    .d_2(undriven_9));  // open: a_2
  comparador comparador_17 (.A(undriven_13), .B(undriven_11), .C(undriven_9), .D(1'b1));  // open: a_2, b_2, c_2, d_2
  comparador comparador_18 (.D(1'b1));  // open: A, B, C, a_2, b_2, c_2, d_2
  comparador comparador_19 (.D(1'b1));  // open: A, B, C, a_2, b_2, c_2, d_2
  comparador comparador_20 (.D(1'b1));  // open: A, B, C, a_2, b_2, c_2, d_2
  comparador comparador_21 (.D(1'b1));  // open: A, B, C, a_2, b_2, c_2, d_2
endmodule

module comparador (
  input  A,
  input  B,
  input  a_2,
  input  C,
  input  D,
  input  b_2,
  input  c_2,
  input  d_2
);

  wire and_1_out, and_2_out, and_3_out, and_4_out, and_5_out, and_6_out, and_7_out, and_8_out, and_9_out,
       and_10_out, and_11_out, and_12_out, and_13_out, not_1_out, not_2_out, not_3_out, not_4_out, not_5_out,
       not_6_out, not_7_out, not_8_out, not_9_out, not_10_out;

  and and_1 (and_1_out, B, D);
  and and_2 (and_2_out, B, C);
  not not_1 (not_1_out, C);
  and and_3 (and_3_out, B, not_1_out, not_2_out);
  not not_2 (not_2_out, D);
  and and_4 (and_4_out, A, D);
  and and_5 (and_5_out, A, C);
  not not_3 (not_3_out, A);
  and and_6 (and_6_out, not_3_out, not_4_out, C);
  not not_4 (not_4_out, B);
  and and_7 (and_7_out, C, D);
  and and_8 (and_8_out, A, not_5_out, not_6_out);
  not not_5 (not_5_out, C);
  not not_6 (not_6_out, D);
  and and_9 (and_9_out, A, B);
  not not_7 (not_7_out, A);
  not not_8 (not_8_out, B);
  and and_10 (and_10_out, not_7_out, not_8_out, D);
  and and_11 (and_11_out, B, C, not_9_out);
  not not_9 (not_9_out, D);
  and and_12 (and_12_out, A, not_10_out);
  not not_10 (not_10_out, D);
  and and_13 (and_13_out, A, B);
  or or_1 (a_2, and_1_out, and_2_out, A);
  or or_2 (b_2, and_3_out, and_4_out, and_5_out);
  or or_3 (c_2, and_6_out, and_7_out, and_8_out, and_9_out);
  or or_4 (d_2, and_10_out, and_11_out, and_12_out, and_13_out);
endmodule
