// Logisim project practica11Parte A.circ as structural Verilog: 1 circuit, main circuit main
module main (
);

  wire and_1_out, and_2_out, clock_1_out, j_k_ff_1_q, j_k_ff_1_qn, j_k_ff_2_q, j_k_ff_2_qn, j_k_ff_3_q,
       j_k_ff_3_qn, or_1_out, or_2_out, or_3_out;

  Clock clock_1 (.out(clock_1_out));
  J_K_Flip_Flop j_k_ff_1 (
    .J(or_3_out), .clk(clock_1_out), .K(j_k_ff_2_qn), .Q(j_k_ff_1_q), .Qn(j_k_ff_1_qn));  // open: preset, en, reset
  J_K_Flip_Flop j_k_ff_2 (
    .J(or_1_out), .clk(clock_1_out), .K(or_2_out), .Q(j_k_ff_2_q), .Qn(j_k_ff_2_qn));  // open: preset, en, reset
  J_K_Flip_Flop j_k_ff_3 (
    .J(j_k_ff_2_qn), .clk(clock_1_out), .K(j_k_ff_1_qn), .Q(j_k_ff_3_q), .Qn(j_k_ff_3_qn));  // open: preset, en, reset
  and and_1 (and_1_out, j_k_ff_2_qn, j_k_ff_3_qn);
  and and_2 (and_2_out, j_k_ff_2_q, j_k_ff_3_q);
  or or_1 (or_1_out, j_k_ff_1_q, j_k_ff_3_qn);
  or or_2 (or_2_out, j_k_ff_3_q, j_k_ff_1_qn);
  or or_3 (or_3_out, and_1_out, and_2_out);
  LED led_1 (.in(j_k_ff_1_qn));
  LED led_2 (.in(j_k_ff_2_qn));
  LED led_3 (.in(j_k_ff_3_qn));
endmodule
